// Logisim project Mabon_CIR.circ as structural Verilog: 1 circuit, main circuit main
module main (
  input  Rst,
  input  ProgramCHK,
  input  Indirect,
  input  C1,
  output S1,
  output S2
);

  wire and_1_out, and_2_out, and_3_out, and_4_out, and_5_out, and_6_out, and_7_out, and_8_out, and_9_out,
       and_10_out, and_11_out, and_12_out, and_13_out, clock_1_out, not_1_out, not_2_out, not_3_out,
       not_4_out, not_5_out, not_6_out, or_1_out, or_2_out, or_3_out, t_ff_2_q, t_ff_2_qn, t_ff_3_q,
       t_ff_3_qn, t_ff_4_q, t_ff_4_qn;

  Clock clock_1 (.out(clock_1_out));
  not not_1 (not_1_out, C1);
  not not_2 (not_2_out, t_ff_2_q);
  and and_1 (and_1_out, not_2_out, t_ff_3_q, not_3_out);
  not not_3 (not_3_out, t_ff_4_q);
  not not_4 (not_4_out, t_ff_3_q);
  and and_2 (and_2_out, t_ff_2_q, not_4_out, not_3_out);
  and and_3 (and_3_out, ProgramCHK, not_2_out, t_ff_3_q);
  and and_4 (and_4_out, not_2_out, t_ff_4_q);
  and and_5 (and_5_out, not_2_out, t_ff_3_q);
  and and_6 (and_6_out, not_1_out, not_2_out, not_5_out, t_ff_4_qn);
  not not_5 (not_5_out, t_ff_3_q);
  and and_7 (and_7_out, not_2_out, t_ff_3_q, not_6_out);
  not not_6 (not_6_out, t_ff_4_qn);
  and and_8 (and_8_out, Indirect, not_2_out, not_6_out);
  or or_1 (or_1_out, and_1_out, and_2_out, and_3_out);
  or or_2 (or_2_out, and_4_out, and_5_out);
  or or_3 (or_3_out, and_6_out, and_7_out, and_8_out);
  T_Flip_Flop t_ff_1 (.T(1'b1), .clk(clock_1_out), .Q(S2), .Qn(S1), .reset(Rst));  // open: preset
  T_Flip_Flop t_ff_2 (.T(or_1_out), .clk(S2), .Q(t_ff_2_q), .Qn(t_ff_2_qn), .reset(Rst));  // open: preset
  T_Flip_Flop t_ff_3 (.T(or_2_out), .clk(S2), .Q(t_ff_3_q), .Qn(t_ff_3_qn), .reset(Rst));  // open: preset
  T_Flip_Flop t_ff_4 (.T(or_3_out), .clk(S2), .Q(t_ff_4_q), .Qn(t_ff_4_qn), .reset(Rst));  // open: preset
  and and_9 (and_9_out, t_ff_2_qn, t_ff_3_qn, t_ff_4_qn);
  and and_10 (and_10_out, t_ff_3_qn, t_ff_4_q, t_ff_2_qn);
  and and_11 (and_11_out, t_ff_3_q, t_ff_2_qn, t_ff_4_qn);
  and and_12 (and_12_out, t_ff_2_qn, t_ff_3_q, t_ff_4_q);
  and and_13 (and_13_out, t_ff_4_qn, t_ff_3_qn, t_ff_2_q);
endmodule
