// Logisim project V_final_state_machine.circ as structural Verilog: 3 circuits, main circuit main
module main (
  input  Reset,
  input  indi_rect,
  input  PC,
  input  C1,
  output S1,
  output S2,
  output Fetch,
  output Decode,
  output Indirect,
  output Excecute,
  output Trap
);

  wire and_1_out, and_2_out, and_3_out, and_4_out, and_5_out, and_6_out, and_7_out, CLK_out, not_1_out,
       or_1_out, or_2_out, or_3_out, tflipflop_2_q, tflipflop_2_qdash, tflipflop_3_q, tflipflop_3_qdash,
       tflipflop_4_q, tflipflop_4_qdash;

  Clock CLK (.out(CLK_out));
  not not_1 (not_1_out, C1);
  and and_1 (and_1_out, tflipflop_4_qdash, not_1_out);
  and and_2 (and_2_out, tflipflop_4_q, indi_rect);
  and and_3 (and_3_out, tflipflop_2_qdash, tflipflop_3_q, PC, tflipflop_4_q);
  and and_4 (and_4_out, tflipflop_2_q, tflipflop_3_qdash, tflipflop_4_qdash);
  and and_5 (and_5_out, tflipflop_2_qdash, tflipflop_3_qdash, tflipflop_4_q);
  and and_6 (and_6_out, tflipflop_2_qdash, tflipflop_3_q, tflipflop_4_q);
  or or_1 (or_1_out, tflipflop_3_q, and_1_out, and_2_out);
  or or_2 (or_2_out, and_3_out, and_4_out);
  tflipflop tflipflop_1 (.T(1'b1), .CLK(CLK_out), .Rst(Reset), .Q(S2), .Qdash(S1));
  or or_3 (or_3_out, and_5_out, and_6_out);
  and and_7 (and_7_out, or_1_out, tflipflop_2_qdash);
  tflipflop tflipflop_2 (.T(or_2_out), .CLK(S2), .Rst(Reset), .Q(tflipflop_2_q), .Qdash(tflipflop_2_qdash));
  tflipflop tflipflop_3 (.T(or_3_out), .CLK(S2), .Rst(Reset), .Q(tflipflop_3_q), .Qdash(tflipflop_3_qdash));
  tflipflop tflipflop_4 (.T(and_7_out), .CLK(S2), .Rst(Reset), .Q(tflipflop_4_q), .Qdash(tflipflop_4_qdash));
  and and_8 (Fetch, tflipflop_2_qdash, tflipflop_3_qdash, tflipflop_4_qdash);
  and and_9 (Decode, tflipflop_2_qdash, tflipflop_3_qdash, tflipflop_4_q);
  and and_10 (Indirect, tflipflop_2_qdash, tflipflop_3_q, tflipflop_3_qdash);
  and and_11 (Trap, tflipflop_2_q, tflipflop_3_qdash, tflipflop_4_qdash);
  and and_12 (Excecute, tflipflop_2_qdash, tflipflop_3_q, tflipflop_4_q);
  // Digital_Oscilloscope digital_oscilloscope_1: pin names not known; wires that end beside it: CLK_out, S1, S2, Fetch, Decode, Indirect, Excecute, Trap
endmodule

module dflipflop (
  input  Clk,
  input  D,
  input  Reset,
  output Q,
  output Qdash
);

  wire and_1_out, and_2_out, and_3_out, and_4_out, and_5_out, and_6_out, not_1_out, not_2_out, not_3_out,
       not_4_out, not_5_out;

  not not_1 (not_1_out, Reset);
  and and_1 (and_1_out, not_5_out, not_3_out);
  not not_2 (not_2_out, and_1_out);
  and and_2 (and_2_out, not_2_out, Clk, not_1_out);
  not not_3 (not_3_out, and_2_out);
  and and_3 (and_3_out, not_3_out, Clk, not_5_out);
  not not_4 (not_4_out, and_3_out);
  and and_4 (and_4_out, not_4_out, D, not_1_out);
  not not_5 (not_5_out, and_4_out);
  and and_5 (and_5_out, not_3_out, Qdash);
  and and_6 (and_6_out, Q, not_4_out, not_1_out);
  not not_6 (Q, and_5_out);
  not not_7 (Qdash, and_6_out);
endmodule

module tflipflop (
  input  T,
  input  CLK,
  input  Rst,
  output Q,
  output Qdash
);

  wire xor_1_out;

  xor xor_1 (xor_1_out, Q, T);
  dflipflop dflipflop_1 (.Clk(CLK), .D(xor_1_out), .Reset(Rst), .Q(Q), .Qdash(Qdash));
endmodule
